# Fritzing sketch schema (saved by Fritzing 0.9.3b)

parts:
  Bauteil1 = Adafruit LIS3DH [part_number="Adafruit #2809"]
  U1 = LIPO-1000mAh [package=lipo-1000]
  ESP1 = Firebeetle ESP32 IOT

nets:
  VIN: Bauteil1.VIN, Bauteil1.3.3V, ESP1.3V3
  GND: Bauteil1.GND, ESP1.GND
  N1: Bauteil1.SCL, ESP1.SCL
  N2: Bauteil1.SDA, ESP1.SDA
  N3: Bauteil1.SDO, ESP1.MISO
  N4: Bauteil1.CS, ESP1.MOSI
  N5: Bauteil1.INT1, ESP1.D4
  N6: U1.+, ESP1.Li-ion_+
  N7: U1.-, ESP1.Li-ion_-

custom parts:
  Adafruit LIS3DH: The LIS3DH is a very popular low power triple-axis accelerometer. It's low-cost, but has just about every 'extra' you'd want in an accelerometer: Three axis sensing, 10-bit precision ±2g/±4g/±8g/±16g selectable scaling Both I2C (2 possible addresses) and SPI interface options Interrupt output Multiple data rate options 1 Hz to 5Khz As low as 2uA current draw (just the chip itself, not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
